# Fritzing sketch Robotics wiring diagram new 2 (saved by Fritzing 0.9.3b)
breadboards: 1

parts:
  Part1 = Arduino Mega 2560 (Rev3)
  U1 = TCRT5000 Line Tracker
  U2 = TCRT5000 Line Tracker

nets:
  N1: Part1.A0, U1.Ao
  N2: Part1.A1, U2.Ao
  N3: Part1.D41, U1.Do
  N4: Part1.D43, U2.Do

notes:
  Power 5V
  Raykha s8

custom parts:
  TCRT5000 Line Tracker: A line tracker module based on TCRT5000 (Vishay)
